// Logisim project ALU-32 Bits.circ as structural Verilog: 3 circuits, main circuit main
module main (
  input  CarryIn,
  input  [4:0] Shifter,
  input  [3:0] CodeOp,
  input  [31:0] in_4,
  input  [31:0] in_5,
  output [31:0] S,
  output [3:0] Flags
);

  wire clock_1_out, clock_2_out;
  wire [31:0] A, B;

  ALU_32_Bits alu_32_bits_1 (
    .CarryIn(CarryIn), .A(A), .B(B), .CodeOp(CodeOp), .Shifter(Shifter), .Flags(Flags), .out_6(S));
  Clock clock_1 (.out(clock_1_out));
  Random #(.width(32)) random_1 (.clk(clock_1_out), .out(A));  // open: next, clr
  Clock clock_2 (.out(clock_2_out));
  Random #(.width(32)) random_2 (.clk(clock_2_out), .out(B));  // open: next, clr
endmodule

module ALU_32_Bits (
  input  CarryIn,
  input  [4:0] Shifter,
  input  [31:0] A,
  input  [31:0] B,
  input  [3:0] CodeOp,
  output [31:0] out_6,
  output [3:0] Flags
);

  wire _0___B_1Bit, A___B_1Bit, A___B_1Bit_t, A___B___CIN_1Bit, A___B___CIN___1_1Bit, adder_1_cout,
       adder_2_cout, adder_3_cout, adder_4_cout, adder_5_cout, adder_6_cout, COUT_2_out, COUT_3_out,
       COUT_4_out, COUT_5_out, COUT_out, decoder_1_out0, decoder_1_out1, decoder_1_out2, decoder_1_out3,
       decoder_1_out4, decoder_1_out7, decoder_1_out8, decoder_1_out12, decoder_1_out13, decoder_1_out14,
       decoder_1_out15;
  wire [31:0] _0___B, A___B, A___B___CIN, A___B___CIN___1, A___B_t, A_AND_B_2_out, A_AND_B_out,
       A_AND_NOT_B_out, A_OR_B_out, A_XOR_B_out, adder_1_out, adder_2_out, adder_3_out, adder_4_out,
       adder_5_out, adder_6_out, and_1_out, and_2_out, and_3_out, ASR_out, B____shift_2_out, B____shift_out,
       bit_extender_1_out, bit_extender_2_out, bit_extender_3_out, bit_extender_4_out, bit_extender_5_out,
       bit_extender_6_out, bit_extender_7_out, bit_extender_8_out, bit_extender_9_out, bit_extender_10_out,
       bit_extender_11_out, bit_extender_12_out, bit_extender_13_out, bit_extender_14_out,
       bit_extender_15_out, bit_extender_16_out, minus_1, MUL_out, multiplier_1_out, negator_2_out,
       not_1_out, not_2_out, NOT_B_out, or_1_out, ROR_out, shifter_1_out, shifter_2_out, shifter_3_out,
       shifter_4_out, xor_1_out;

  Decoder #(.select(4), .enable("false")) decoder_1 (
    .out0(decoder_1_out0), .out1(decoder_1_out1), .out2(decoder_1_out2), .out3(decoder_1_out3),
    .out4(decoder_1_out4), .out5(A___B___CIN_1Bit), .out6(A___B___CIN___1_1Bit), .out7(decoder_1_out7),
    .out8(decoder_1_out8), .out9(_0___B_1Bit), .out10(A___B_1Bit_t), .out11(A___B_1Bit),
    .out12(decoder_1_out12), .out13(decoder_1_out13), .out14(decoder_1_out14), .out15(decoder_1_out15),
    .sel(CodeOp));
  assign bit_extender_1_out = {{31{decoder_1_out0}}, decoder_1_out0};  // Bit_Extender bit_extender_1
  Negator #(.width(32)) negator_1 (.in(32'h1), .out(minus_1));
  assign bit_extender_2_out = {{31{decoder_1_out12}}, decoder_1_out12};  // Bit_Extender bit_extender_2
  assign bit_extender_3_out = {{31{decoder_1_out1}}, decoder_1_out1};  // Bit_Extender bit_extender_3
  assign bit_extender_4_out = {{31{decoder_1_out14}}, decoder_1_out14};  // Bit_Extender bit_extender_4
  assign and_1_out = A & B;  // AND_Gate and_1, 32 bits wide
  assign bit_extender_5_out = {{31{decoder_1_out15}}, decoder_1_out15};  // Bit_Extender bit_extender_5
  assign or_1_out = A | B;  // OR_Gate or_1, 32 bits wide
  assign xor_1_out = A ^ B;  // XOR_Gate xor_1, 32 bits wide
  assign A_AND_B_out = and_1_out & bit_extender_1_out;  // AND_Gate A_AND_B, 32 bits wide
  assign A_OR_B_out = or_1_out & bit_extender_2_out;  // AND_Gate A_OR_B, 32 bits wide
  assign bit_extender_6_out = {{31{decoder_1_out8}}, decoder_1_out8};  // Bit_Extender bit_extender_6
  assign not_1_out = ~B;  // NOT_Gate not_1, 32 bits wide
  assign and_2_out = A & not_1_out;  // AND_Gate and_2, 32 bits wide
  assign A_XOR_B_out = xor_1_out & bit_extender_3_out;  // AND_Gate A_XOR_B, 32 bits wide
  assign bit_extender_7_out = {{31{A___B_1Bit}}, A___B_1Bit};  // Bit_Extender bit_extender_7
  assign not_2_out = ~B;  // NOT_Gate not_2, 32 bits wide
  assign A_AND_NOT_B_out = and_2_out & bit_extender_4_out;  // AND_Gate A_AND_NOT_B, 32 bits wide
  assign NOT_B_out = not_2_out & bit_extender_5_out;  // AND_Gate NOT_B, 32 bits wide
  assign bit_extender_8_out = {{31{A___B___CIN_1Bit}}, A___B___CIN_1Bit};  // Bit_Extender bit_extender_8
  assign and_3_out = A & B;  // AND_Gate and_3, 32 bits wide
  assign A_AND_B_2_out = and_3_out & bit_extender_6_out;  // AND_Gate A_AND_B_2, 32 bits wide
  assign bit_extender_9_out = {{31{A___B___CIN___1_1Bit}}, A___B___CIN___1_1Bit};  // Bit_Extender bit_extender_9
  Adder #(.width(32)) adder_1 (.a(A), .b(B), .out(adder_1_out), .cout(adder_1_cout));  // open: cin
  assign bit_extender_10_out = {{31{_0___B_1Bit}}, _0___B_1Bit};  // Bit_Extender bit_extender_10
  Adder #(.width(32)) adder_2 (.a(A), .b(B), .out(adder_2_out), .cin(CarryIn), .cout(adder_2_cout));
  assign A___B = adder_1_out & bit_extender_7_out;  // AND_Gate A___B, 32 bits wide
  and COUT (COUT_out, adder_1_cout, A___B_1Bit);
  assign bit_extender_11_out = {{31{A___B_1Bit_t}}, A___B_1Bit_t};  // Bit_Extender bit_extender_11
  assign A___B___CIN = adder_2_out & bit_extender_8_out;  // AND_Gate A___B___CIN, 32 bits wide
  and COUT_2 (COUT_2_out, adder_2_cout, A___B___CIN_1Bit);
  assign bit_extender_12_out = {{31{decoder_1_out13}}, decoder_1_out13};  // Bit_Extender bit_extender_12
  Negator #(.width(32)) negator_2 (.in(B), .out(negator_2_out));
  Adder #(.width(32)) adder_3 (.a(A), .b(negator_2_out), .out(adder_3_out), .cin(CarryIn), .cout(adder_3_cout));
  assign bit_extender_13_out = {{31{decoder_1_out2}}, decoder_1_out2};  // Bit_Extender bit_extender_13
  Adder #(.width(32)) adder_4 (
    .a(adder_3_out), .b(minus_1), .out(adder_4_out), .cin(adder_3_cout), .cout(adder_4_cout));
  assign bit_extender_14_out = {{31{decoder_1_out3}}, decoder_1_out3};  // Bit_Extender bit_extender_14
  assign bit_extender_15_out = {{31{decoder_1_out4}}, decoder_1_out4};  // Bit_Extender bit_extender_15
  Adder #(.width(32)) adder_5 (.a({32{1'b0}}), .b(negator_2_out), .out(adder_5_out), .cout(adder_5_cout));  // open: cin
  assign A___B___CIN___1 = adder_4_out & bit_extender_9_out;  // AND_Gate A___B___CIN___1, 32 bits wide
  and COUT_3 (COUT_3_out, adder_4_cout, A___B___CIN___1_1Bit);
  assign bit_extender_16_out = {{31{decoder_1_out7}}, decoder_1_out7};  // Bit_Extender bit_extender_16
  Adder #(.width(32)) adder_6 (.a(A), .b(negator_2_out), .out(adder_6_out), .cout(adder_6_cout));  // open: cin
  assign _0___B = adder_5_out & bit_extender_10_out;  // AND_Gate _0___B, 32 bits wide
  and COUT_4 (COUT_4_out, adder_5_cout, _0___B_1Bit);
  Multiplier #(.width(32)) multiplier_1 (.a(A), .b(B), .out(multiplier_1_out));  // open: cin, cout
  assign A___B_t = adder_6_out & bit_extender_11_out;  // AND_Gate A___B_2, 32 bits wide
  and COUT_5 (COUT_5_out, adder_6_cout, A___B_1Bit_t);
  Shifter #(.width(32)) shifter_1 (.in(B), .\dist (Shifter), .out(shifter_1_out));
  assign MUL_out = multiplier_1_out & bit_extender_12_out;  // AND_Gate MUL, 32 bits wide
  assign B____shift_out = shifter_1_out & bit_extender_13_out;  // AND_Gate B____shift, 32 bits wide
  Shifter #(.width(32), .shift("lr")) shifter_2 (.in(B), .\dist (Shifter), .out(shifter_2_out));
  assign B____shift_2_out = shifter_2_out & bit_extender_14_out;  // AND_Gate B____shift_2, 32 bits wide
  Shifter #(.width(32), .shift("ar")) shifter_3 (.in(B), .\dist (Shifter), .out(shifter_3_out));
  assign ASR_out = shifter_3_out & bit_extender_15_out;  // AND_Gate ASR, 32 bits wide
  Shifter #(.width(32), .shift("rr")) shifter_4 (.in(B), .\dist (Shifter), .out(shifter_4_out));
  assign ROR_out = shifter_4_out & bit_extender_16_out;  // AND_Gate ROR, 32 bits wide
  assign out_6 = A_AND_B_out | A_OR_B_out | A_XOR_B_out | A_AND_NOT_B_out | NOT_B_out | A_AND_B_2_out | A___B | A___B___CIN | A___B___CIN___1 | _0___B | A___B_t | MUL_out | B____shift_out | B____shift_2_out | ASR_out | ROR_out;  // OR_Gate S, 32 bits wide
  Comparator #(.width(32)) comparator_1 (.a(out_6), .b({32{1'b0}}), .eq(Flags[3]), .lt(Flags[2]));  // open: gt
  or or_2 (Flags[0], COUT_out, COUT_2_out, COUT_3_out, COUT_4_out, COUT_5_out);
  V_Flag v_flag_1 (
    .A(A), .B(B), .A___B(A___B), .A___B___CIN(A___B___CIN), .A___B___CIN___1(A___B___CIN___1),
    ._0___B(_0___B), .A___B_2(A___B_t), .is_A_B(A___B_1Bit), .is_A_B_CIN(A___B___CIN_1Bit),
    .is_A_B_CIN_1(A___B___CIN___1_1Bit), .is_0_B(_0___B_1Bit), .is_A_B_2(A___B_1Bit_t), .V(Flags[1]));

  // Other names for the same wires on the sheet: C = Flags[0]; V = Flags[1]; N = Flags[2]; Z = Flags[3];
  //   S[31:0] = out_6
endmodule

// V-FLag
module V_Flag (
  input  [31:0] A,
  input  [31:0] B,
  input  [31:0] A___B,
  input  [31:0] A___B___CIN,
  input  [31:0] A___B___CIN___1,
  input  [31:0] _0___B,
  input  [31:0] A___B_2,
  input  is_A_B,
  input  is_A_B_CIN,
  input  is_A_B_CIN_1,
  input  is_0_B,
  input  is_A_B_2,
  output V
);

  wire _0___B_Sign, A___B___CIN___1_Sign, A___B___CIN_Sign, A___B_Sign, A___B_Sign_t, A___B_Sign_t_t, A_Sign,
       and_1_out, and_2_out, and_3_out, and_4_out, and_5_out, and_6_out, and_7_out, and_8_out, and_9_out,
       and_10_out, B_Sign, comparator_5_gt, comparator_5_lt, comparator_7_gt, comparator_7_lt,
       comparator_9_gt, comparator_9_lt, comparator_11_gt, comparator_11_lt, comparator_13_gt,
       comparator_13_lt, not_1_out, not_2_out, not_3_out, or_1_out, or_2_out, or_3_out, or_4_out, or_5_out;

  Comparator #(.width(32)) comparator_1 (.a(A), .b({32{1'b0}}), .lt(A_Sign));  // open: gt, eq
  Comparator #(.width(32)) comparator_2 (.a(B), .b({32{1'b0}}), .lt(B_Sign));  // open: gt, eq
  Comparator #(.width(1)) comparator_3 (.a(A_Sign), .b(B_Sign), .eq(A___B_Sign_t_t));  // open: gt, lt
  Comparator #(.width(32)) comparator_4 (.a(A___B), .b({32{1'b0}}), .lt(A___B_Sign));  // open: gt, eq
  Comparator #(.width(1)) comparator_5 (
    .a(A___B_Sign), .b(A_Sign), .gt(comparator_5_gt), .lt(comparator_5_lt));  // open: eq
  or or_1 (or_1_out, comparator_5_gt, comparator_5_lt);
  and and_1 (and_1_out, or_1_out, A___B_Sign_t_t);
  and and_2 (and_2_out, and_1_out, is_A_B);
  Comparator #(.width(32)) comparator_6 (.a(A___B___CIN), .b({32{1'b0}}), .lt(A___B___CIN_Sign));  // open: gt, eq
  Comparator #(.width(1)) comparator_7 (
    .a(A___B___CIN_Sign), .b(A_Sign), .gt(comparator_7_gt), .lt(comparator_7_lt));  // open: eq
  or or_2 (or_2_out, comparator_7_gt, comparator_7_lt);
  and and_3 (and_3_out, or_2_out, A___B_Sign_t_t);
  and and_4 (and_4_out, and_3_out, is_A_B_CIN);
  Comparator #(.width(32)) comparator_8 (
    .a(A___B___CIN___1), .b({32{1'b0}}), .lt(A___B___CIN___1_Sign));  // open: gt, eq
  or or_3 (or_3_out, comparator_9_gt, comparator_9_lt);
  Comparator #(.width(1)) comparator_9 (
    .a(A___B___CIN___1_Sign), .b(A_Sign), .gt(comparator_9_gt), .lt(comparator_9_lt));  // open: eq
  not not_1 (not_1_out, A___B_Sign_t_t);
  and and_5 (and_5_out, or_3_out, not_1_out);
  and and_6 (and_6_out, and_5_out, is_A_B_CIN_1);
  Comparator #(.width(32)) comparator_10 (.a(_0___B), .b({32{1'b0}}), .lt(_0___B_Sign));  // open: gt, eq
  Comparator #(.width(1)) comparator_11 (
    .a(_0___B_Sign), .b(A_Sign), .gt(comparator_11_gt), .lt(comparator_11_lt));  // open: eq
  or or_4 (or_4_out, comparator_11_gt, comparator_11_lt);
  not not_2 (not_2_out, A___B_Sign_t_t);
  and and_7 (and_7_out, or_4_out, not_2_out);
  and and_8 (and_8_out, and_7_out, is_0_B);
  Comparator #(.width(32)) comparator_12 (.a(A___B_2), .b({32{1'b0}}), .lt(A___B_Sign_t));  // open: gt, eq
  Comparator #(.width(1)) comparator_13 (
    .a(A___B_Sign_t), .b(A_Sign), .gt(comparator_13_gt), .lt(comparator_13_lt));  // open: eq
  or or_5 (or_5_out, comparator_13_gt, comparator_13_lt);
  not not_3 (not_3_out, A___B_Sign_t_t);
  and and_9 (and_9_out, or_5_out, not_3_out);
  and and_10 (and_10_out, and_9_out, is_A_B_2);
  or or_6 (V, and_2_out, and_4_out, and_6_out, and_8_out, and_10_out);
endmodule
