// Logisim project Projet_PEP.circ as structural Verilog: 1 circuit, main circuit main
module main (
  input  CarryIn,
  input  [4:0] Shifter,
  input  [3:0] CodeOp,
  input  [31:0] DataIn,
  input  in_5,
  input  [2:0] RegA,
  input  [2:0] RegB,
  input  [2:0] RegDest,
  output [3:0] out_9
);

  wire button_1_out, button_2_out;
  wire [31:0] alu_32_bits_1_out_6, main_1_aout, main_1_bout, multiplexer_1_out;

  Button button_1 (.out(button_1_out));
  Button button_2 (.out(button_2_out));
  Multiplexer #(.width(32), .enable("false")) multiplexer_1 (
    .in0(alu_32_bits_1_out_6), .in1(DataIn), .out(multiplexer_1_out), .sel(in_5));
  Banc_registre_main main_1 (
    .RegA(RegA), .RegB(RegB), .DataIn(multiplexer_1_out), .RegtDest(RegDest), .Clk(button_1_out),
    .Reset(button_2_out), .Aout(main_1_aout), .Bout(main_1_bout));
  ALU_32_Bits alu_32_bits_1 (
    .CarryIn(CarryIn), .Shifter(Shifter), .A(main_1_aout), .B(main_1_bout), .CodeOp(CodeOp), .Flags(out_9),
    .out_6(alu_32_bits_1_out_6));
endmodule
