// Logisim project RAM.circ as structural Verilog: 1 circuit, main circuit RAM
module RAM (
  input  [7:0] Address,
  input  [31:0] Datain,
  input  sel,
  input  Ld,
  input  Clr,
  output [31:0] Dataout
);

  wire clk_out;

  Clock clk (.out(clk_out));
  RAM_part #(.dataWidth(32), .bus("separate")) ram_1 (
    .addr(Address), .din(Datain), .data(Dataout), .sel(sel), .clk(clk_out), .ld(Ld), .clr(Clr));  // open: str
endmodule
