// Logisim project ALU-32 Bits.circ as structural Verilog: 3 circuits, main circuit main
module main (
  input  CarryIn,
  input  [3:0] CodeOp,
  input  [4:0] Shifter,
  input  [31:0] in_4,
  input  [31:0] in_5,
  output [31:0] S,
  output [3:0] Flags
);

  wire clock_1_out, clock_2_out;
  wire [31:0] A, B;

  Clock clock_1 (.out(clock_1_out));
  Clock clock_2 (.out(clock_2_out));
  ALU_32_Bits alu_32_bits_1 (
    .CarryIn(CarryIn), .A(A), .B(B), .Shifter(Shifter), .CodeOp(CodeOp), .Flags(Flags), .out_6(S));
  Random #(.width(32)) random_1 (.clk(clock_1_out), .out(A));  // open: next, clr
  Random #(.width(32)) random_2 (.clk(clock_2_out), .out(B));  // open: next, clr
endmodule

module ALU_32_Bits (
  input  CarryIn,
  input  [4:0] Shifter,
  input  [31:0] A,
  input  [31:0] B,
  input  [3:0] CodeOp,
  output [31:0] out_6,
  output [3:0] Flags
);

  wire A_B_CarryOut, A_B_CarryOut_t, A_B_CIN_1_CarryOut, A_B_CIN_1_Overflow, A_B_CIN_CarryOut,
       A_B_CIN_Overflow, A_B_Overflow, A_B_Overflow_t, adder_3_cout;
  wire [31:0] adder_1_out, adder_2_out, adder_3_out, adder_4_out, adder_5_out, and_1_out, and_2_out,
       and_3_out, minus_1, multiplier_1_out, negator_2_out, negator_3_out, negator_4_out, not_1_out,
       not_2_out, or_1_out, shifter_1_out, shifter_2_out, shifter_3_out, shifter_4_out, xor_1_out;

  assign and_1_out = A & B;  // AND_Gate and_1, 32 bits wide
  Negator #(.width(32)) negator_1 (.in(32'h1), .out(minus_1));
  assign or_1_out = A | B;  // OR_Gate or_1, 32 bits wide
  assign xor_1_out = A ^ B;  // XOR_Gate xor_1, 32 bits wide
  assign not_1_out = ~B;  // NOT_Gate not_1, 32 bits wide
  assign and_2_out = A & not_1_out;  // AND_Gate and_2, 32 bits wide
  assign not_2_out = ~B;  // NOT_Gate not_2, 32 bits wide
  assign and_3_out = A & B;  // AND_Gate and_3, 32 bits wide
  Adder #(.width(32)) adder_1 (.a(A), .b(B), .out(adder_1_out), .cout(A_B_CarryOut));  // open: cin
  Adder #(.width(32)) adder_2 (.a(A), .b(B), .out(adder_2_out), .cin(CarryIn), .cout(A_B_CIN_CarryOut));
  V_Flag v_flag_1 (.A(A), .B(B), .Resultat(adder_1_out), .Overflow(A_B_Overflow));
  Negator #(.width(32)) negator_2 (.in(B), .out(negator_2_out));
  Adder #(.width(32)) adder_3 (.a(A), .b(negator_2_out), .out(adder_3_out), .cin(CarryIn), .cout(adder_3_cout));
  V_Flag v_flag_2 (.A(A), .B(B), .Resultat(adder_2_out), .Overflow(A_B_CIN_Overflow));
  Adder #(.width(32)) adder_4 (
    .a(adder_3_out), .b(minus_1), .out(adder_4_out), .cin(adder_3_cout), .cout(A_B_CIN_1_CarryOut));
  Adder #(.width(32)) adder_5 (.a(A), .b(negator_2_out), .out(adder_5_out), .cout(A_B_CarryOut_t));  // open: cin
  Multiplier #(.width(32)) multiplier_1 (.a(A), .b(B), .out(multiplier_1_out));  // open: cin, cout
  Negator #(.width(32)) negator_3 (.in(B), .out(negator_3_out));
  Shifter #(.width(32)) shifter_1 (.in(B), .\dist (Shifter), .out(shifter_1_out));
  V_Flag v_flag_3 (.A(A), .B(negator_3_out), .Resultat(adder_4_out), .Overflow(A_B_CIN_1_Overflow));
  Shifter #(.width(32), .shift("lr")) shifter_2 (.in(B), .\dist (Shifter), .out(shifter_2_out));
  Shifter #(.width(32), .shift("ar")) shifter_3 (.in(B), .\dist (Shifter), .out(shifter_3_out));
  Negator #(.width(32)) negator_4 (.in(B), .out(negator_4_out));
  Shifter #(.width(32), .shift("rr")) shifter_4 (.in(B), .\dist (Shifter), .out(shifter_4_out));
  V_Flag v_flag_4 (.A(A), .B(negator_4_out), .Resultat(adder_5_out), .Overflow(A_B_Overflow_t));
  Multiplexer #(.select(4)) multiplexer_1 (
    .in5(A_B_CIN_Overflow), .in6(A_B_CIN_1_Overflow), .in10(A_B_Overflow_t), .in11(A_B_Overflow),
    .out(Flags[1]), .sel(CodeOp));  // open: in0, in1, in2, in3, in4, in7, in8, in9, in12, in13, in14, in15, en
  Multiplexer #(.select(4)) multiplexer_2 (
    .in5(A_B_CIN_CarryOut), .in6(A_B_CIN_1_CarryOut), .in10(A_B_CarryOut_t), .in11(A_B_CarryOut),
    .out(Flags[0]), .sel(CodeOp));  // open: in0, in1, in2, in3, in4, in7, in8, in9, in12, in13, in14, in15, en
  Multiplexer #(.select(4), .width(32)) multiplexer_3 (
    .in0(and_1_out), .in1(xor_1_out), .in2(shifter_1_out), .in3(shifter_2_out), .in4(shifter_3_out),
    .in5(adder_2_out), .in6(adder_4_out), .in7(shifter_4_out), .in8(and_3_out), .in9(negator_2_out),
    .in10(adder_5_out), .in11(adder_1_out), .in12(or_1_out), .in13(multiplier_1_out), .in14(and_2_out),
    .in15(not_2_out), .out(out_6), .sel(CodeOp));  // open: en
  Comparator #(.width(32)) comparator_1 (.a(out_6), .b({32{1'b0}}), .eq(Flags[3]), .lt(Flags[2]));  // open: gt

  // Other names for the same wires on the sheet: C = Flags[0]; V = Flags[1]; N = Flags[2]; Z = Flags[3];
  //   S[31:0] = out_6
endmodule

// V-FLag
module V_Flag (
  input  [31:0] Resultat,
  input  [31:0] A,
  input  [31:0] B,
  output Overflow
);

  wire and_1_out, and_2_out, bitselector_1_out, bitselector_2_out, bitselector_3_out;

  BitSelector #(.width(32)) bitselector_1 (.in(Resultat), .out(bitselector_1_out), .sel({5{1'b1}}));
  BitSelector #(.width(32)) bitselector_2 (.in(A), .out(bitselector_2_out), .sel({5{1'b1}}));
  BitSelector #(.width(32)) bitselector_3 (.in(B), .out(bitselector_3_out), .sel({5{1'b1}}));
  and and_1 (and_1_out, ~bitselector_2_out, ~bitselector_3_out, bitselector_1_out);  // AND_Gate
  and and_2 (and_2_out, bitselector_2_out, bitselector_3_out, ~bitselector_1_out);  // AND_Gate
  or or_1 (Overflow, and_1_out, and_2_out);
endmodule
