// Logisim project Banc_registre.circ as structural Verilog: 2 circuits, main circuit main
module main (
);

  wire button_1_out, button_2_out, button_3_out, button_4_out, clock_1_out;
  wire [2:0] regIn_out, selA_out, selB_out;
  wire [31:0] banc_registre_1_aout, banc_registre_1_bout, Data_out;

  Button button_1 (.out(button_1_out));
  Button button_2 (.out(button_2_out));
  Button button_3 (.out(button_3_out));
  Clock clock_1 (.out(clock_1_out));
  Button button_4 (.out(button_4_out));
  Random #(.width(3), .seed(5)) selA (.clk(button_1_out), .out(selA_out));  // open: next, clr
  Random #(.width(3)) selB (.clk(button_1_out), .out(selB_out));  // open: next, clr
  Random #(.width(32)) Data (.clk(button_2_out), .out(Data_out));  // open: next, clr
  Random #(.width(3)) regIn (.clk(button_3_out), .out(regIn_out));  // open: next, clr
  // Probe on banc_registre_1_bout
  // Probe on Data_out
  Banc_Registre banc_registre_1 (
    .DataIn(Data_out), .RegtDest(regIn_out), .RegA(selA_out), .RegB(selB_out), .Clk(clock_1_out),
    .Reset(button_4_out), .Aout(banc_registre_1_aout), .Bout(banc_registre_1_bout));
  // Probe on banc_registre_1_aout
endmodule

module Banc_Registre (
  input  [2:0] RegA,
  input  [2:0] RegB,
  input  [31:0] DataIn,
  input  [2:0] RegtDest,
  input  Clk,
  input  Reset,
  output [31:0] Aout,
  output [31:0] Bout
);

  wire and_1_out, and_2_out, and_3_out, and_4_out, and_5_out, and_6_out, and_7_out, and_8_out,
       decoder_1_out0, decoder_1_out1, decoder_1_out2, decoder_1_out3, decoder_1_out4, decoder_1_out5,
       decoder_1_out6, decoder_1_out7;
  wire [31:0] R0_q, R1_q, R2_q, R3_q, R4_q, R5_q, R6_q, R7_q;

  Decoder #(.select(3)) decoder_1 (
    .out0(decoder_1_out0), .out1(decoder_1_out1), .out2(decoder_1_out2), .out3(decoder_1_out3),
    .out4(decoder_1_out4), .out5(decoder_1_out5), .out6(decoder_1_out6), .out7(decoder_1_out7), .sel(RegtDest));  // open: en
  and and_1 (and_1_out, decoder_1_out0, Clk);
  Multiplexer #(.select(3), .width(32)) multiplexer_1 (
    .in0(R0_q), .in1(R1_q), .in2(R2_q), .in3(R3_q), .in4(R4_q), .in5(R5_q), .in6(R6_q), .in7(R7_q),
    .out(Aout), .sel(RegA));  // open: en
  Register #(.width(32)) R0 (.D(DataIn), .Q(R0_q), .clk(and_1_out), .clr(Reset));  // open: en
  Register #(.width(32)) R1 (.D(DataIn), .Q(R1_q), .clk(and_2_out), .clr(Reset));  // open: en
  and and_2 (and_2_out, decoder_1_out1, Clk);
  Multiplexer #(.select(3), .width(32)) multiplexer_2 (
    .in0(R0_q), .in1(R1_q), .in2(R2_q), .in3(R3_q), .in4(R4_q), .in5(R5_q), .in6(R6_q), .in7(R7_q),
    .out(Bout), .sel(RegB));  // open: en
  Register #(.width(32)) R2 (.D(DataIn), .Q(R2_q), .clk(and_3_out), .clr(Reset));  // open: en
  and and_3 (and_3_out, decoder_1_out2, Clk);
  Register #(.width(32)) R3 (.D(DataIn), .Q(R3_q), .clk(and_4_out), .clr(Reset));  // open: en
  and and_4 (and_4_out, decoder_1_out3, Clk);
  Register #(.width(32)) R4 (.D(DataIn), .Q(R4_q), .clk(and_5_out), .clr(Reset));  // open: en
  and and_5 (and_5_out, decoder_1_out4, Clk);
  Register #(.width(32)) R5 (.D(DataIn), .Q(R5_q), .clk(and_6_out), .clr(Reset));  // open: en
  and and_6 (and_6_out, decoder_1_out5, Clk);
  Register #(.width(32)) R6 (.D(DataIn), .Q(R6_q), .clk(and_8_out), .clr(Reset));  // open: en
  and and_7 (and_7_out, decoder_1_out7, Clk);
  and and_8 (and_8_out, decoder_1_out6, Clk);
  Register #(.width(32)) R7 (.D(DataIn), .Q(R7_q), .clk(and_7_out), .clr(Reset));  // open: en
endmodule
