// Logisim project Controleur.circ as structural Verilog
module Controller (
  input  [15:0] Instructions,
  input  Clk,
  input  Reset,
  input  [3:0] Flags,
  output Load_0_Store_1,
  output [3:0] CodeOp,
  output [7:0] PC,
  output [2:0] Rm,
  output [4:0] Imm5,
  output [2:0] Rd,
  output [7:0] Imm8,
  output [2:0] Rn
);

  wire category_a_1_load, category_c_1_load_0_store_1;
  wire [1:0] category_selector_1_category;
  wire [2:0] category_a_1_rd, category_a_1_rm, category_a_1_rn, category_b_1_rega, category_b_1_regb,
       category_b_1_regd, category_c_1_rd, category_c_1_rn;
  wire [3:0] category_a_1_codop, category_b_1_codeop;
  wire [4:0] category_a_1_imm5;
  wire [7:0] BasicPC, category_a_1_imm8, category_c_1_imm8, category_d_1_pc, register_1_q, register_2_q;

  Category_Selector category_selector_1 (.Instruction(Instructions), .Category(category_selector_1_category));
  Category_A category_a_1 (
    .Instruction(Instructions), .Load(category_a_1_load), .Rm(category_a_1_rm), .Rd(category_a_1_rd),
    .Rn(category_a_1_rn), .CODOP(category_a_1_codop), .Imm5(category_a_1_imm5), .Imm8(category_a_1_imm8));
  Category_B category_b_1 (
    .Instruction(Instructions), .CodeOp(category_b_1_codeop), .RegA(category_b_1_rega),
    .RegD(category_b_1_regd), .RegB(category_b_1_regb));
  Category_C category_c_1 (
    .Instruction(Instructions), .Load_0_Store_1(category_c_1_load_0_store_1), .Rd(category_c_1_rd),
    .Imm8(category_c_1_imm8), .Rn(category_c_1_rn));
  Category_D category_d_1 (.Instruction(Instructions), .Flags(Flags), .PC(category_d_1_pc));
  Multiplexer #(.select(2), .width(3)) multiplexer_1 (
    .in0(category_a_1_rm), .in1(category_b_1_rega), .out(Rm), .sel(category_selector_1_category));  // open: in2, in3, en
  Multiplexer #(.select(2), .width(3)) multiplexer_2 (
    .in0(category_a_1_rd), .in1(category_b_1_regd), .in2(category_c_1_rd), .out(Rd),
    .sel(category_selector_1_category));  // open: in3, en
  Multiplexer #(.select(2), .width(3)) multiplexer_3 (
    .in0(category_a_1_rn), .in1(category_b_1_regb), .in2(category_c_1_rn), .out(Rn),
    .sel(category_selector_1_category));  // open: in3, en
  Multiplexer #(.select(2), .width(4)) multiplexer_4 (
    .in0(category_a_1_codop), .in1(category_b_1_codeop), .out(CodeOp), .sel(category_selector_1_category));  // open: in2, in3, en
  Multiplexer #(.select(2), .width(5)) multiplexer_5 (
    .in0(category_a_1_imm5), .out(Imm5), .sel(category_selector_1_category));  // open: in1, in2, in3, en
  Multiplexer #(.select(2), .width(8)) multiplexer_6 (
    .in0(category_a_1_imm8), .in2(category_c_1_imm8), .out(Imm8), .sel(category_selector_1_category));  // open: in1, in3, en
  Multiplexer #(.select(2)) multiplexer_7 (
    .in0(category_a_1_load), .in2(category_c_1_load_0_store_1), .out(Load_0_Store_1),
    .sel(category_selector_1_category));  // open: in1, in3, en
  Multiplexer #(.select(2), .width(8)) multiplexer_8 (
    .in0(BasicPC), .in1(BasicPC), .in2(BasicPC), .in3(category_d_1_pc), .out(PC),
    .sel(category_selector_1_category));  // open: en
  Register register_1 (.D(8'h1), .Q(register_1_q), .clk(Clk), .clr(Reset));  // open: en
  Register register_2 (.D(PC), .Q(register_2_q), .clk(Clk), .clr(Reset));  // open: en
  Adder adder_1 (.a(register_1_q), .b(register_2_q), .out(BasicPC));  // open: cin, cout

  // Other names for the same wires on the sheet: CurrentPC[7:0] = PC
endmodule

module Cond (
  input  Bit3_Cond,
  input  Bit2_Cond,
  input  Bit1_Cond,
  input  Bit0_Cond,
  input  Z,
  input  N,
  input  V,
  input  C,
  output Cond
);

  wire and_1_out, and_2_out, and_3_out, and_4_out, and_5_out, and_6_out, and_7_out, and_8_out, and_9_out,
       and_10_out, and_11_out, and_12_out, and_13_out, and_14_out, comparator_1_eq, comparator_2_eq,
       comparator_3_eq, comparator_4_eq, decoder_1_out0, decoder_1_out1, decoder_1_out2, decoder_1_out3,
       decoder_1_out4, decoder_1_out5, decoder_1_out6, decoder_1_out7, decoder_1_out8, decoder_1_out9,
       decoder_1_out10, decoder_1_out11, decoder_1_out12, decoder_1_out13, decoder_1_out14;

  Decoder #(.select(4)) decoder_1 (
    .out0(decoder_1_out0), .out1(decoder_1_out1), .out2(decoder_1_out2), .out3(decoder_1_out3),
    .out4(decoder_1_out4), .out5(decoder_1_out5), .out6(decoder_1_out6), .out7(decoder_1_out7),
    .out8(decoder_1_out8), .out9(decoder_1_out9), .out10(decoder_1_out10), .out11(decoder_1_out11),
    .out12(decoder_1_out12), .out13(decoder_1_out13), .out14(decoder_1_out14),
    .sel({Bit3_Cond, Bit2_Cond, Bit1_Cond, Bit0_Cond}));  // open: out15, en
  Comparator #(.width(1)) comparator_1 (.a(N), .b(V), .eq(comparator_1_eq));  // open: gt, lt
  Comparator #(.width(1)) comparator_2 (.a(N), .b(V), .eq(comparator_2_eq));  // open: gt, lt
  Comparator #(.width(1)) comparator_3 (.a(N), .b(V), .eq(comparator_3_eq));  // open: gt, lt
  Comparator #(.width(1)) comparator_4 (.a(N), .b(V), .eq(comparator_4_eq));  // open: gt, lt
  and and_1 (and_1_out, decoder_1_out0, Z);
  and and_2 (and_2_out, decoder_1_out1, ~Z);  // AND_Gate
  and and_3 (and_3_out, decoder_1_out2, C);
  and and_4 (and_4_out, decoder_1_out3, ~C);  // AND_Gate
  and and_5 (and_5_out, decoder_1_out4, N);
  and and_6 (and_6_out, decoder_1_out5, ~N);  // AND_Gate
  and and_7 (and_7_out, decoder_1_out6, V);
  and and_8 (and_8_out, decoder_1_out7, ~V);  // AND_Gate
  and and_9 (and_9_out, decoder_1_out8, C, ~Z);  // AND_Gate
  and and_10 (and_10_out, decoder_1_out9, ~C, Z);  // AND_Gate
  and and_11 (and_11_out, decoder_1_out10, comparator_1_eq);
  and and_12 (and_12_out, decoder_1_out11, ~comparator_2_eq);  // AND_Gate
  and and_13 (and_13_out, decoder_1_out12, ~Z, comparator_3_eq);  // AND_Gate
  and and_14 (and_14_out, decoder_1_out13, Z, ~comparator_4_eq);  // AND_Gate
  or or_1 (Cond, and_1_out, and_2_out, and_3_out, and_4_out, and_5_out, and_6_out, and_7_out, and_8_out, and_9_out, and_10_out, and_11_out, and_12_out, and_13_out, and_14_out, decoder_1_out14);
endmodule

module Category_A (
  input  [15:0] Instruction,
  output Load,
  output [2:0] Rm,
  output [2:0] Rd,
  output [2:0] Rn,
  output [3:0] CODOP,
  output [4:0] Imm5,
  output [7:0] Imm8
);

  wire decoder_1_out0, decoder_1_out1, decoder_1_out2, decoder_2_out12, decoder_2_out13, decoder_2_out14,
       Load_ON, Rm_ON;
  wire [2:0] priority_encoder_1_out;

  Decoder #(.select(3)) decoder_1 (
    .out0(decoder_1_out0), .out1(decoder_1_out1), .out2(decoder_1_out2), .out4(Load_ON),
    .sel(Instruction[13:11]));  // open: out3, out5, out6, out7, en
  Multiplexer #(.select(3), .width(4)) multiplexer_1 (
    .in0(4'b0010), .in1(4'b0011), .in2(4'b0100), .in3(4'b1011), .in4(4'b1010), .in5(4'b1011), .out(CODOP),
    .sel(priority_encoder_1_out));  // open: in6, in7, en
  Priority_Encoder priority_encoder_1 (
    .in0(decoder_1_out0), .in1(decoder_1_out1), .in2(decoder_1_out2), .in3(Load_ON), .in4(decoder_2_out12),
    .in5(decoder_2_out13), .in6(decoder_2_out14), .out(priority_encoder_1_out));  // open: in7, en_in, gs, en_out
  or or_1 (Rm_ON, decoder_2_out14, decoder_2_out13, decoder_2_out12);
  Decoder #(.select(5)) decoder_2 (
    .out12(decoder_2_out12), .out13(decoder_2_out13), .out14(decoder_2_out14), .sel(Instruction[13:9]));  // open: out0, out1, out2, out3, out4, out5, out6, out7, out8, out9, out10, out11, out15, out16, out17, out18, out19, out20, out21, out22, out23, out24, out25, out26, out27, out28, out29, out30, out31, en
  Multiplexer #(.width(3)) multiplexer_2 (
    .in0(Instruction[5:3]), .in1(Instruction[8:6]), .out(Rm), .sel(Rm_ON));  // open: en
  Multiplexer #(.width(3)) multiplexer_3 (
    .in0(Instruction[2:0]), .in1(Instruction[10:8]), .out(Rd), .sel(Load_ON));  // open: en
  Multiplexer multiplexer_4 (.in1(1'b0), .out(Load), .sel(Load_ON));  // open: in0, en

  assign Imm5 = Instruction[10:6];
  assign Imm8 = Instruction[7:0];
  assign Rn = Instruction[5:3];

  // Other names for the same wires on the sheet: _5BitCodeOp[4:0] = Instruction[13:9]; B_Rd[2:0] = Instruction[10:8];
  //   _3BitCodeOp[2:0] = Instruction[13:11]; B_Rm[2:0] = Instruction[8:6]; CodeOp[3:0] = CODOP;
  //   L_Rd[2:0] = Instruction[2:0]; Rd_ON = Load_ON; S_Rm[2:0] = Instruction[5:3]
endmodule

module Category_B (
  input  [15:0] Instruction,
  output [3:0] CodeOp,
  output [2:0] RegA,
  output [2:0] RegD,
  output [2:0] RegB
);

  wire decoder_1_out0, decoder_1_out1, decoder_1_out2, decoder_1_out3, decoder_1_out4, decoder_1_out5,
       decoder_1_out6, decoder_1_out7, decoder_1_out12, decoder_1_out13, decoder_1_out14, InvRegARegB, NoRm,
       NoRn, RD_RN;
  wire [2:0] bit_extender_1_out, bit_extender_2_out, RegA_t, RegB_t;

  Decoder #(.select(4)) decoder_1 (
    .out0(decoder_1_out0), .out1(decoder_1_out1), .out2(decoder_1_out2), .out3(decoder_1_out3),
    .out4(decoder_1_out4), .out5(decoder_1_out5), .out6(decoder_1_out6), .out7(decoder_1_out7), .out9(NoRm),
    .out12(decoder_1_out12), .out13(decoder_1_out13), .out14(decoder_1_out14), .out15(NoRn),
    .sel({Instruction[6], Instruction[7], Instruction[8], Instruction[9]}));  // open: out8, out10, out11, en
  or or_1 (InvRegARegB, NoRm, decoder_1_out13);
  or or_2 (RD_RN, decoder_1_out0, decoder_1_out1, decoder_1_out2, decoder_1_out3, decoder_1_out4, decoder_1_out5, decoder_1_out6, decoder_1_out7, decoder_1_out12, decoder_1_out13, decoder_1_out14);
  assign bit_extender_1_out = {{2{NoRm}}, NoRm};  // Bit_Extender bit_extender_1
  assign bit_extender_2_out = {{2{NoRn}}, NoRn};  // Bit_Extender bit_extender_2
  assign RegA = RegA_t & bit_extender_1_out;  // AND_Gate and_1, 3 bits wide
  assign RegB = RegB_t;  // AND_Gate and_2, 3 bits wide AND_Gate
  Multiplexer #(.width(3)) multiplexer_1 (
    .in1({Instruction[0], Instruction[1], Instruction[2]}), .out(RegD), .sel(RD_RN));  // open: in0, en
  Multiplexer #(.width(3)) multiplexer_2 (
    .in0({Instruction[3], Instruction[4], Instruction[5]}),
    .in1({Instruction[0], Instruction[1], Instruction[2]}), .out(RegA_t), .sel(InvRegARegB));  // open: en
  Multiplexer #(.width(3)) multiplexer_3 (
    .in0({Instruction[0], Instruction[1], Instruction[2]}),
    .in1({Instruction[3], Instruction[4], Instruction[5]}), .out(RegB_t), .sel(InvRegARegB));  // open: en

  assign CodeOp = {Instruction[6], Instruction[7], Instruction[8], Instruction[9]};

  // Other names for the same wires on the sheet: RegM_N[2:0] = {Instruction[3], Instruction[4], Instruction[5]};
  //   RegM_N_D[2:0] = {Instruction[0], Instruction[1], Instruction[2]}
endmodule

module Category_C (
  input  [15:0] Instruction,
  output Load_0_Store_1,
  output [2:0] Rd,
  output [7:0] Imm8,
  output [2:0] Rn
);

  Multiplexer #(.width(3)) multiplexer_1 (
    .in0({Instruction[8], Instruction[9], Instruction[10]}), .out(Rd), .sel(Instruction[11]));  // open: in1, en
  Multiplexer #(.width(3)) multiplexer_2 (
    .in1({Instruction[8], Instruction[9], Instruction[10]}), .out(Rn), .sel(Instruction[11]));  // open: in0, en

  assign Imm8 = {Instruction[0], Instruction[1], Instruction[2], Instruction[3], Instruction[4], Instruction[5], Instruction[6], Instruction[7]};
  assign Load_0_Store_1 = Instruction[11];

  // Other names for the same wires on the sheet: Rt[2:0] = {Instruction[8], Instruction[9], Instruction[10]};
  //   Ld_St = Instruction[11]
endmodule

module Category_D (
  input  [15:0] Instruction,
  input  [3:0] Flags,
  output [7:0] PC
);

  wire cond_1_cond;
  wire [7:0] multiplexer_1_out;

  Cond cond_1 (
    .Bit3_Cond(Instruction[11]), .Bit2_Cond(Instruction[10]), .Bit1_Cond(Instruction[9]),
    .Bit0_Cond(Instruction[8]), .Z(Flags[3]), .N(Flags[2]), .V(Flags[1]), .C(Flags[0]), .Cond(cond_1_cond));
  Multiplexer #(.width(8)) multiplexer_1 (
    .in0(8'h1), .in1(Instruction[7:0]), .out(multiplexer_1_out), .sel(cond_1_cond));  // open: en
  Adder adder_1 (.a(multiplexer_1_out), .b(8'h1), .out(PC));  // open: cin, cout
endmodule

module Category_Selector (
  input  [15:0] Instruction,
  output [1:0] Category
);

  wire and_1_out, and_2_out, and_3_out, nand_1_out;

  nand nand_1 (nand_1_out, Instruction[15], Instruction[14]);
  and and_1 (and_1_out, ~Instruction[15], Instruction[14], ~Instruction[13], ~Instruction[12], ~Instruction[11], ~Instruction[10]);  // AND_Gate
  and and_2 (and_2_out, ~Instruction[15], Instruction[14], Instruction[13], ~Instruction[12]);  // AND_Gate
  and and_3 (and_3_out, Instruction[15], Instruction[14], ~Instruction[13], Instruction[12]);  // AND_Gate
  Priority_Encoder #(.select(2)) priority_encoder_1 (
    .in0(nand_1_out), .in1(and_1_out), .in2(and_2_out), .in3(and_3_out), .out(Category));  // open: gs, en_out, en_in
endmodule

module Old_Controller (
  input  [15:0] Instructions,
  input  Clock,
  input  Reset,
  input  [3:0] Flags,
  output [7:0] Program_Counter,
  output _0_Load__1_Store,
  output [3:0] Codop_de_l_ALU,
  output [2:0] Registre_Rm,
  output [2:0] Registre_Rd,
  output [2:0] Registre_Rn,
  output [7:0] Imm8,
  output [4:0] Imm5,
  output [2:0] Imm3
);

  wire ADC, AND, and_4_out, and_10_out, and_11_out, and_24_out, and_25_out, and_26_out, and_31_out, ASR, BIC,
       Branch, Branch_8, CMN, CMP, CMP_out, DATA_PROCESSING_out, EOR, LDR_out, LSL, LSR, MOV_out, MUL, MVN,
       nand_1_out, nand_2_out, nand_3_out, nand_4_out, nand_5_out, nand_6_out, nand_7_out, nand_8_out,
       nand_9_out, nand_10_out, or_2_out, or_3_out, or_4_out, or_5_out, or_6_out, or_7_out, or_8_out,
       or_9_out, ORR, ROR, RSB, SBC, STR_out, TST;
  wire [1:1] LSL_out, LSR_out;
  wire [2:0] _5_REG_0, _5_REG_CMP, _5_REG_LDR_STR, _5_REG_MOV, _7_IMM_3, _7_REG, and_2_out, and_3_out,
       and_5_out, and_12_out, and_13_out, and_15_out, and_16_out, and_17_out, and_18_out, and_19_out,
       and_20_out, and_21_out, and_22_out, and_27_out, and_28_out, and_29_out, and_30_out, DataProc1,
       DataProc2, DataProc3, DataProc4;
  wire [2:2] ASR_out;
  wire [3:0] _5_CodeOp, _7_CodeOp, and_7_out, and_8_out, and_9_out, and_14_out, and_33_out, and_34_out,
       bit_extender_9_out, or_1_out, or_10_out;
  wire [3:3] ADD_REG_out, SUB_out;
  wire [4:0] _5_IMM_5;
  wire [7:0] _5_IMM_8, multiplexer_1_out;

  nand u_LSL (LSL_out[1], Instructions[11], Instructions[12], Instructions[13], Instructions[14], Instructions[15]);
  nand nand_1 (nand_1_out, Instructions[11], Instructions[12], Instructions[13], Instructions[14]);
  and u_LSR (LSR_out[1], Instructions[11], nand_1_out);
  assign Imm5 = Instructions[10:6] & _5_IMM_5;  // AND_Gate and_1, 5 bits wide
  assign and_2_out = Instructions[5:3] & _5_REG_0;  // AND_Gate and_2, 3 bits wide
  assign and_3_out = Instructions[2:0] & _5_REG_0;  // AND_Gate and_3, 3 bits wide
  nand nand_2 (nand_2_out, Instructions[11], Instructions[13], Instructions[14], Instructions[15]);
  and u_ASR (ASR_out[2], Instructions[12], nand_2_out);
  and MOV (MOV_out, Instructions[13], nand_3_out);
  and and_4 (and_4_out, Instructions[13], Instructions[11]);
  nand nand_3 (nand_3_out, Instructions[11], Instructions[12], Instructions[14], Instructions[15]);
  and u_CMP (CMP_out, and_4_out, nand_5_out);
  assign and_5_out = Instructions[10:8] & _5_REG_MOV;  // AND_Gate and_5, 3 bits wide
  assign Imm8 = Instructions[7:0] & _5_IMM_8;  // AND_Gate and_6, 8 bits wide
  nand nand_4 (nand_4_out, Instructions[14], Instructions[13]);
  nand nand_5 (nand_5_out, Instructions[12], Instructions[14], Instructions[15]);
  assign and_7_out = {2'b00, LSL_out[1], 1'b0} & _5_CodeOp;  // AND_Gate and_7, 4 bits wide
  assign and_8_out = {2'b00, {2{LSR_out[1]}}} & _5_CodeOp;  // AND_Gate and_8, 4 bits wide
  assign and_9_out = {1'b0, ASR_out[2], 2'b00} & _5_CodeOp;  // AND_Gate and_9, 4 bits wide
  and and_10 (and_10_out, Instructions[15], Instructions[12], Instructions[11]);
  and LDR (LDR_out, nand_4_out, and_10_out);
  assign or_1_out = and_7_out | and_8_out | and_9_out;  // OR_Gate or_1, 4 bits wide
  and and_11 (and_11_out, Instructions[15], Instructions[12]);
  nand nand_6 (nand_6_out, Instructions[14], Instructions[13]);
  and STR (STR_out, nand_6_out, and_11_out);
  assign and_12_out = Instructions[10:8] & _5_REG_CMP;  // AND_Gate and_12, 3 bits wide
  or or_2 (or_2_out, LSL_out[1], LSR_out[1], ASR_out[2]);
  or or_3 (or_3_out, CMP_out, MOV_out, LDR_out, STR_out);
  or or_4 (or_4_out, LSL_out[1], LSR_out[1], ASR_out[2]);
  or or_5 (or_5_out, LDR_out, STR_out);
  assign _5_REG_0 = {{2{or_2_out}}, or_2_out};  // Bit_Extender bit_extender_1
  assign _5_IMM_5 = {{4{or_2_out}}, or_2_out};  // Bit_Extender bit_extender_2
  assign _5_IMM_8 = {{7{or_3_out}}, or_3_out};  // Bit_Extender bit_extender_3
  assign _5_REG_MOV = {{2{MOV_out}}, MOV_out};  // Bit_Extender bit_extender_4
  assign _5_REG_CMP = {{2{CMP_out}}, CMP_out};  // Bit_Extender bit_extender_5
  assign _5_CodeOp = {{3{or_4_out}}, or_4_out};  // Bit_Extender bit_extender_6
  assign _5_REG_LDR_STR = {{2{or_5_out}}, or_5_out};  // Bit_Extender bit_extender_7
  Bit_Extender #(.in_width(3), .out_width(1), .\type ("sign")) bit_extender_8 (.in(and_13_out), .out(_0_Load__1_Store));
  assign and_13_out = Instructions[10:8] & _5_REG_LDR_STR;  // AND_Gate and_13, 3 bits wide
  and DATA_PROCESSING (DATA_PROCESSING_out, Instructions[14], nand_7_out);
  nand nand_7 (nand_7_out, Instructions[10], Instructions[11], Instructions[12], Instructions[13], Instructions[14], Instructions[15]);
  assign bit_extender_9_out = {{3{DATA_PROCESSING_out}}, DATA_PROCESSING_out};  // Bit_Extender bit_extender_9
  assign and_14_out = Instructions[9:6] & bit_extender_9_out;  // AND_Gate and_14, 4 bits wide
  Decoder #(.select(4)) decoder_1 (
    .out0(AND), .out1(EOR), .out2(LSL), .out3(LSR), .out4(ASR), .out5(ADC), .out6(SBC), .out7(ROR),
    .out8(TST), .out9(RSB), .out10(CMP), .out11(CMN), .out12(ORR), .out13(MUL), .out14(BIC), .out15(MVN),
    .sel(and_14_out));  // open: en
  assign and_15_out = {Instructions[3], Instructions[4], Instructions[5]} & DataProc1;  // AND_Gate and_15, 3 bits wide
  assign and_16_out = {Instructions[0], Instructions[1], Instructions[2]} & DataProc1;  // AND_Gate and_16, 3 bits wide
  assign and_17_out = {Instructions[3], Instructions[4], Instructions[5]} & DataProc2;  // AND_Gate and_17, 3 bits wide
  assign and_18_out = {Instructions[0], Instructions[1], Instructions[2]} & DataProc2;  // AND_Gate and_18, 3 bits wide
  assign and_19_out = {Instructions[3], Instructions[4], Instructions[5]} & DataProc3;  // AND_Gate and_19, 3 bits wide
  assign and_20_out = {Instructions[0], Instructions[1], Instructions[2]} & DataProc3;  // AND_Gate and_20, 3 bits wide
  assign DataProc1 = {{2{or_6_out}}, or_6_out};  // Bit_Extender bit_extender_10
  or or_6 (or_6_out, AND, EOR, LSL, LSR, ASR, ADC, SBC, ROR, ORR, MVN);
  or or_7 (or_7_out, TST, CMP, CMN);
  assign DataProc2 = {{2{or_7_out}}, or_7_out};  // Bit_Extender bit_extender_11
  assign DataProc3 = {{2{RSB}}, RSB};  // Bit_Extender bit_extender_12
  assign DataProc4 = {{2{MUL}}, MUL};  // Bit_Extender bit_extender_13
  assign and_21_out = {Instructions[3], Instructions[4], Instructions[5]} & DataProc4;  // AND_Gate and_21, 3 bits wide
  assign and_22_out = {Instructions[0], Instructions[1], Instructions[2]} & DataProc4;  // AND_Gate and_22, 3 bits wide
  and and_23 (Branch, Instructions[12], ~Instructions[13], Instructions[14], Instructions[15]);  // AND_Gate
  Cond cond_1 (
    .Bit3_Cond(Instructions[11]), .Bit2_Cond(Instructions[10]), .Bit1_Cond(Instructions[9]),
    .Bit0_Cond(Instructions[8]), .Z(Flags[3]), .N(Flags[2]), .V(Flags[1]), .C(Flags[0]), .Cond(Branch_8));
  and and_24 (and_24_out, Branch_8, Branch);
  Multiplexer #(.width(8)) multiplexer_1 (
    .in0(8'h1), .in1(Instructions[7:0]), .out(multiplexer_1_out), .sel(and_24_out));  // open: en
  Register register_1 (.D(multiplexer_1_out), .Q(Program_Counter), .clk(Clock), .clr(Reset));  // open: en
  and and_25 (and_25_out, Instructions[11], Instructions[12]);
  and ADD_REG (ADD_REG_out[3], and_25_out, nand_8_out);
  and and_26 (and_26_out, Instructions[9], Instructions[11], Instructions[12]);
  nand nand_8 (nand_8_out, Instructions[9], Instructions[10], Instructions[13], Instructions[14], Instructions[15]);
  assign and_27_out = _7_REG & ~_7_IMM_3;  // AND_Gate and_27, 3 bits wide
  assign and_28_out = {Instructions[3], Instructions[4], Instructions[5]} & _7_REG;  // AND_Gate and_28, 3 bits wide
  assign and_29_out = {Instructions[0], Instructions[1], Instructions[2]} & _7_REG;  // AND_Gate and_29, 3 bits wide
  nand nand_9 (nand_9_out, Instructions[10], Instructions[13], Instructions[14], Instructions[15]);
  and SUB (SUB_out[3], and_26_out, nand_9_out);
  assign and_30_out = {Instructions[6], Instructions[7], Instructions[8]} & and_27_out;  // AND_Gate and_30, 3 bits wide
  and and_31 (and_31_out, Instructions[10], Instructions[11], Instructions[12]);
  nand nand_10 (nand_10_out, Instructions[9], Instructions[13], Instructions[14], Instructions[15]);
  and ADD_IMM (ADD_REG_out[3], and_31_out, nand_10_out);
  assign Imm3 = {Instructions[6], Instructions[7], Instructions[8]} & _7_IMM_3;  // AND_Gate and_32, 3 bits wide
  or or_8 (or_8_out, ADD_REG_out[3], SUB_out[3], ADD_REG_out[3]);
  or or_9 (or_9_out, ADD_REG_out[3], SUB_out[3], ADD_REG_out[3]);
  assign and_33_out = {ADD_REG_out[3], 1'b0, {2{ADD_REG_out[3]}}} & _7_CodeOp;  // AND_Gate and_33, 4 bits wide
  assign and_34_out = {SUB_out[3], 1'b0, SUB_out[3], 1'b0} & _7_CodeOp;  // AND_Gate and_34, 4 bits wide
  assign _7_REG = {{2{or_8_out}}, or_8_out};  // Bit_Extender bit_extender_14
  assign _7_IMM_3 = {{2{ADD_REG_out[3]}}, ADD_REG_out[3]};  // Bit_Extender bit_extender_15
  assign _7_CodeOp = {{3{or_9_out}}, or_9_out};  // Bit_Extender bit_extender_16
  assign or_10_out = and_33_out | and_34_out;  // OR_Gate or_10, 4 bits wide
  assign Registre_Rm = and_2_out | and_15_out | and_17_out | and_22_out | and_30_out;  // OR_Gate or_11, 3 bits wide
  assign Registre_Rd = and_3_out | and_5_out | and_16_out | and_13_out | and_20_out | and_22_out | and_29_out;  // OR_Gate or_12, 3 bits wide
  assign Registre_Rn = and_12_out | and_18_out | and_19_out | and_21_out | and_13_out | and_16_out | and_28_out;  // OR_Gate or_13, 3 bits wide
  assign Codop_de_l_ALU = or_1_out | and_14_out | or_10_out;  // OR_Gate or_14, 4 bits wide

  // Other names for the same wires on the sheet: I_10 = Instructions[10]; Instr[15:0] = Instructions;
  //   I_9 = Instructions[9]; I_5 = Instructions[5]; I_4 = Instructions[4]; I_3 = Instructions[3];
  //   I_2 = Instructions[2]; I_1 = Instructions[1]; I_0 = Instructions[0]; I_8 = Instructions[8];
  //   I_7 = Instructions[7]; I_6 = Instructions[6]; Clk = Clock; Codop[3:0] = Codop_de_l_ALU; I_11 = Instructions[11];
  //   I_12 = Instructions[12]; I_13 = Instructions[13]; I_14 = Instructions[14]; I_15 = Instructions[15];
  //   Load_Store = _0_Load__1_Store; PC[7:0] = Program_Counter; Rd[2:0] = Registre_Rd; Rm[2:0] = Registre_Rm;
  //   Rn[2:0] = Registre_Rn

  // Notes on the sheet:
  //   INPUTS
  //   5-Bits CodeOp, Contains Category A and Category C instructions
  //   OUTPUTS
  //   6-Bits CodeOp, Contains Category B instructions (Data Processing)
  //   4-Bits CodeOp, Contains Category D instructions (Branch)
  //   7-Bits CodeOp, Contains (Some instrcutions of) Category A
endmodule
