// Logisim project Controleur_bis.circ as structural Verilog: 3 circuits, main circuit main
module main (
  input  [15:0] Instructions,
  input  Clock,
  input  Reset,
  output [7:0] Program_Counter,
  output _0_Load__1_Store,
  output [3:0] Codop_de_l_ALU,
  output [2:0] Registre_Rm,
  output [2:0] Registre_Rd,
  output [2:0] Registre_Rn,
  output [7:0] Immediat_sur_8_bits,
  output [4:0] Imm5
);

  wire _00xxxx, and_1_out, nand_2_out;

  nand nand_1 (_00xxxx, Instructions[15], Instructions[14]);
  nand nand_2 (nand_2_out, Instructions[11], Instructions[12], Instructions[13]);
  and and_1 (and_1_out, nand_2_out, _00xxxx);

  assign Imm5 = Instructions[10:6];
  assign Registre_Rd = Instructions[2:0];
  assign Registre_Rm = Instructions[5:3];

  // Other names for the same wires on the sheet: Clk = Clock; Codop[3:0] = Codop_de_l_ALU; I_6 = Instructions[6];
  //   Instr[15:0] = Instructions; I_7 = Instructions[7]; I_8 = Instructions[8]; I_9 = Instructions[9];
  //   I_10 = Instructions[10]; Imm8[7:0] = Immediat_sur_8_bits; I_11 = Instructions[11]; I_12 = Instructions[12];
  //   I_13 = Instructions[13]; I_14 = Instructions[14]; I_15 = Instructions[15]; Load_Store = _0_Load__1_Store;
  //   PC[7:0] = Program_Counter; I_0 = Instructions[0]; Rd[2:0] = Instructions[2:0]; I_1 = Instructions[1];
  //   I_2 = Instructions[2]; I_3 = Instructions[3]; Rm[2:0] = Instructions[5:3]; I_4 = Instructions[4];
  //   I_5 = Instructions[5]; Rn[2:0] = Registre_Rn

  // Notes on the sheet:
  //   INPUTS
  //   OUTPUTS
endmodule

module Controller (
  input  [15:0] Instructions,
  input  Clock,
  input  Reset,
  input  [3:0] Flags,
  output [7:0] Program_Counter,
  output _0_Load__1_Store,
  output [3:0] Codop_de_l_ALU,
  output [2:0] Registre_Rm,
  output [2:0] Registre_Rd,
  output [2:0] Registre_Rn,
  output [7:0] Immediat_sur_8_bits,
  output [4:0] Imm5
);

  wire ADC, AND, and_4_out, and_10_out, and_11_out, ASR, BIC, Branch, Branch_8, CMN, CMP, CMP_out,
       DATA_PROCESSING_out, EOR, LDR_out, LSL, LSR, MOV_out, MUL, MVN, nand_1_out, nand_2_out, nand_3_out,
       nand_4_out, nand_5_out, nand_6_out, nand_7_out, or_2_out, or_3_out, or_4_out, or_5_out, or_6_out,
       or_7_out, ORR, ROR, RSB, SBC, STR_out, TST;
  wire [1:1] LSL_out, LSR_out;
  wire [2:0] _5_REG_0, _5_REG_CMP, _5_REG_CMP_t, _5_REG_LDR_STR, _5_REG_MOV, and_2_out, and_3_out, and_5_out,
       and_12_out, and_13_out, and_15_out, and_16_out, and_17_out, and_18_out, and_19_out, and_20_out,
       and_21_out, and_22_out, and_23_out, and_24_out, DataProc1, DataProc2, DataProc3, DataProc4, DataProc5;
  wire [2:2] ASR_out;
  wire [3:0] _5_CodeOp, and_7_out, and_8_out, and_9_out, and_14_out, bit_extender_9_out, or_1_out;
  wire [4:0] _5_IMM_5, and_1_out;
  wire [7:0] _5_IMM_8, adder_1_out, adder_2_out, and_6_out, multiplexer_1_out, PC_Cond, register_1_q,
       register_2_q, register_3_q;

  nand u_LSL (LSL_out[1], Instructions[11], Instructions[12], Instructions[13], Instructions[14], Instructions[15]);
  nand nand_1 (nand_1_out, Instructions[11], Instructions[12], Instructions[13], Instructions[14]);
  and u_LSR (LSR_out[1], Instructions[11], nand_1_out);
  assign and_1_out = Instructions[10:6] & _5_IMM_5;  // AND_Gate and_1, 5 bits wide
  assign and_2_out = Instructions[5:3] & _5_REG_0;  // AND_Gate and_2, 3 bits wide
  assign and_3_out = Instructions[2:0] & _5_REG_0;  // AND_Gate and_3, 3 bits wide
  nand nand_2 (nand_2_out, Instructions[11], Instructions[13], Instructions[14], Instructions[15]);
  and u_ASR (ASR_out[2], Instructions[12], nand_2_out);
  and MOV (MOV_out, Instructions[13], nand_3_out);
  and and_4 (and_4_out, Instructions[13], Instructions[11]);
  nand nand_3 (nand_3_out, Instructions[11], Instructions[12], Instructions[14], Instructions[15]);
  and u_CMP (CMP_out, and_4_out, nand_4_out);
  assign and_5_out = Instructions[10:8] & _5_REG_MOV;  // AND_Gate and_5, 3 bits wide
  assign and_6_out = Instructions[7:0] & _5_IMM_8;  // AND_Gate and_6, 8 bits wide
  nand nand_4 (nand_4_out, Instructions[12], Instructions[14], Instructions[15]);
  nand nand_5 (nand_5_out, Instructions[14], Instructions[13]);
  assign and_7_out = {2'b00, LSL_out[1], 1'b0} & _5_CodeOp;  // AND_Gate and_7, 4 bits wide
  assign and_8_out = {2'b00, {2{LSR_out[1]}}} & _5_CodeOp;  // AND_Gate and_8, 4 bits wide
  assign and_9_out = {1'b0, ASR_out[2], 2'b00} & _5_CodeOp;  // AND_Gate and_9, 4 bits wide
  and and_10 (and_10_out, Instructions[15], Instructions[12], Instructions[11]);
  and LDR (LDR_out, nand_5_out, and_10_out);
  assign or_1_out = and_7_out | and_8_out | and_9_out;  // OR_Gate or_1, 4 bits wide
  and and_11 (and_11_out, Instructions[15], Instructions[12]);
  nand nand_6 (nand_6_out, Instructions[14], Instructions[13]);
  and STR (STR_out, nand_6_out, and_11_out);
  assign and_12_out = Instructions[10:8] & _5_REG_CMP_t;  // AND_Gate and_12, 3 bits wide
  or or_2 (or_2_out, LSL_out[1], LSR_out[1], ASR_out[2]);
  or or_3 (or_3_out, CMP_out, MOV_out, LDR_out, STR_out);
  or or_4 (or_4_out, LSL_out[1], LSR_out[1], ASR_out[2]);
  or or_5 (or_5_out, LDR_out, STR_out);
  assign _5_REG_0 = {{2{or_2_out}}, or_2_out};  // Bit_Extender bit_extender_1
  assign _5_IMM_5 = {{4{or_2_out}}, or_2_out};  // Bit_Extender bit_extender_2
  assign _5_IMM_8 = {{7{or_3_out}}, or_3_out};  // Bit_Extender bit_extender_3
  assign _5_REG_MOV = {{2{MOV_out}}, MOV_out};  // Bit_Extender bit_extender_4
  assign _5_REG_CMP = {{2{CMP_out}}, CMP_out};  // Bit_Extender bit_extender_5
  assign _5_CodeOp = {{3{or_4_out}}, or_4_out};  // Bit_Extender bit_extender_6
  assign _5_REG_LDR_STR = {{2{or_5_out}}, or_5_out};  // Bit_Extender bit_extender_7
  assign and_13_out = Instructions[10:8] & _5_REG_LDR_STR;  // AND_Gate and_13, 3 bits wide
  Bit_Extender #(.in_width(3), .out_width(1), .\type ("sign")) bit_extender_8 (.in(and_13_out), .out(_0_Load__1_Store));
  and DATA_PROCESSING (DATA_PROCESSING_out, Instructions[14], nand_7_out);
  nand nand_7 (nand_7_out, Instructions[10], Instructions[11], Instructions[12], Instructions[13], Instructions[14], Instructions[15]);
  assign bit_extender_9_out = {{3{DATA_PROCESSING_out}}, DATA_PROCESSING_out};  // Bit_Extender bit_extender_9
  assign and_14_out = Instructions[9:6] & bit_extender_9_out;  // AND_Gate and_14, 4 bits wide
  Decoder #(.select(4)) decoder_1 (
    .out0(AND), .out1(EOR), .out2(LSL), .out3(LSR), .out4(ASR), .out5(ADC), .out6(SBC), .out7(ROR),
    .out8(TST), .out9(RSB), .out10(CMP), .out11(CMN), .out12(ORR), .out13(MUL), .out14(BIC), .out15(MVN),
    .sel(and_14_out));  // open: en
  assign and_15_out = {Instructions[3], Instructions[4], Instructions[5]} & DataProc1;  // AND_Gate and_15, 3 bits wide
  assign and_16_out = {Instructions[0], Instructions[1], Instructions[2]} & DataProc1;  // AND_Gate and_16, 3 bits wide
  assign and_17_out = {Instructions[3], Instructions[4], Instructions[5]} & DataProc2;  // AND_Gate and_17, 3 bits wide
  assign and_18_out = {Instructions[0], Instructions[1], Instructions[2]} & DataProc2;  // AND_Gate and_18, 3 bits wide
  assign and_19_out = {Instructions[3], Instructions[4], Instructions[5]} & DataProc3;  // AND_Gate and_19, 3 bits wide
  assign and_20_out = {Instructions[0], Instructions[1], Instructions[2]} & DataProc3;  // AND_Gate and_20, 3 bits wide
  assign and_21_out = {Instructions[3], Instructions[4], Instructions[5]} & DataProc4;  // AND_Gate and_21, 3 bits wide
  assign and_22_out = {Instructions[0], Instructions[1], Instructions[2]} & DataProc4;  // AND_Gate and_22, 3 bits wide
  assign DataProc1 = {{2{or_6_out}}, or_6_out};  // Bit_Extender bit_extender_10
  or or_6 (or_6_out, AND, EOR, LSL, LSR, ASR, ADC, SBC, ROR, ORR, MVN);
  assign DataProc2 = {{2{TST}}, TST};  // Bit_Extender bit_extender_11
  assign DataProc3 = {{2{RSB}}, RSB};  // Bit_Extender bit_extender_12
  or or_7 (or_7_out, CMP, CMN);
  assign DataProc4 = {{2{or_7_out}}, or_7_out};  // Bit_Extender bit_extender_13
  assign DataProc5 = {{2{MUL}}, MUL};  // Bit_Extender bit_extender_14
  assign and_23_out = {Instructions[3], Instructions[4], Instructions[5]} & DataProc5;  // AND_Gate and_23, 3 bits wide
  assign and_24_out = {Instructions[0], Instructions[1], Instructions[2]} & DataProc5;  // AND_Gate and_24, 3 bits wide
  and and_25 (Branch, Instructions[12], ~Instructions[13], Instructions[14], Instructions[15]);  // AND_Gate
  Cond cond_1 (
    .Bit3_Cond(Instructions[11]), .Bit2_Cond(Instructions[10]), .Bit1_Cond(Instructions[9]),
    .Bit0_Cond(Instructions[8]), .Z(Flags[3]), .N(Flags[2]), .V(Flags[1]), .C(Flags[0]), .Cond(Branch_8));
  Register register_1 (.D(8'h1), .Q(register_1_q), .clk(Clock));  // open: en, clr
  Register register_2 (.D(Program_Counter), .Q(register_2_q), .clk(Clock));  // open: en, clr
  Multiplexer #(.width(8)) multiplexer_1 (
    .in0(8'h1), .in1(Instructions[7:0]), .out(multiplexer_1_out), .sel(Branch_8));  // open: en
  Adder adder_1 (.a(register_1_q), .b(register_2_q), .out(adder_1_out));  // open: cin, cout
  Register register_3 (.D(multiplexer_1_out), .Q(register_3_q), .clk(Clock));  // open: en, clr
  Multiplexer #(.width(8)) multiplexer_2 (
    .in0(adder_1_out), .in1(PC_Cond), .out(Program_Counter), .sel(Branch));  // open: en
  Adder adder_2 (.a(Program_Counter), .b(register_3_q), .out(adder_2_out));  // open: cin, cout
  Register register_4 (.D(adder_2_out), .Q(PC_Cond), .clk(Clock));  // open: en, clr
  assign Imm5 = and_1_out;  // OR_Gate or_8, 5 bits wide OR_Gate
  assign Immediat_sur_8_bits = and_6_out;  // OR_Gate or_9, 8 bits wide OR_Gate
  assign Codop_de_l_ALU = or_1_out | and_14_out;  // OR_Gate or_10, 4 bits wide
  assign Registre_Rm = and_2_out | and_15_out | and_17_out | and_23_out | and_24_out;  // OR_Gate or_11, 3 bits wide
  assign Registre_Rd = and_3_out | and_5_out | and_16_out | and_13_out | and_20_out | and_22_out | and_24_out;  // OR_Gate or_12, 3 bits wide
  assign Registre_Rn = and_12_out | and_18_out | and_19_out | and_21_out | and_13_out | and_16_out;  // OR_Gate or_13, 3 bits wide

  // Other names for the same wires on the sheet: I_10 = Instructions[10]; Instr[15:0] = Instructions;
  //   I_8 = Instructions[8]; I_9 = Instructions[9]; I_0 = Instructions[0]; I_1 = Instructions[1];
  //   I_2 = Instructions[2]; I_3 = Instructions[3]; I_4 = Instructions[4]; I_5 = Instructions[5];
  //   I_6 = Instructions[6]; I_7 = Instructions[7]; Clk = Clock; Codop[3:0] = Codop_de_l_ALU;
  //   Imm8[7:0] = Immediat_sur_8_bits; I_11 = Instructions[11]; I_12 = Instructions[12]; I_13 = Instructions[13];
  //   I_14 = Instructions[14]; I_15 = Instructions[15]; Load_Store = _0_Load__1_Store; Last_PC[7:0] = Program_Counter;
  //   PC[7:0] = Program_Counter; Rd[2:0] = Registre_Rd; Rm[2:0] = Registre_Rm; Rn[2:0] = Registre_Rn

  // Notes on the sheet:
  //   INPUTS
  //   5-Bits CodeOp, Contains Category A and Category C instructions
  //   OUTPUTS
  //   6-Bits CodeOp, Contains Category B instructions (Data Processing)
  //   4-Bits CodeOp, Contains Category D instructions (Branch)
endmodule

module Cond (
  input  Bit3_Cond,
  input  Bit2_Cond,
  input  Bit1_Cond,
  input  Bit0_Cond,
  input  Z,
  input  N,
  input  V,
  input  C,
  output Cond
);

  wire and_1_out, and_2_out, and_3_out, and_4_out, and_5_out, and_6_out, and_7_out, and_8_out, and_9_out,
       and_10_out, and_11_out, and_12_out, and_13_out, and_14_out, comparator_1_eq, comparator_2_eq,
       comparator_3_eq, comparator_4_eq, decoder_1_out0, decoder_1_out1, decoder_1_out2, decoder_1_out3,
       decoder_1_out4, decoder_1_out5, decoder_1_out6, decoder_1_out7, decoder_1_out8, decoder_1_out9,
       decoder_1_out10, decoder_1_out11, decoder_1_out12, decoder_1_out13, decoder_1_out14;

  Decoder #(.select(4)) decoder_1 (
    .out0(decoder_1_out0), .out1(decoder_1_out1), .out2(decoder_1_out2), .out3(decoder_1_out3),
    .out4(decoder_1_out4), .out5(decoder_1_out5), .out6(decoder_1_out6), .out7(decoder_1_out7),
    .out8(decoder_1_out8), .out9(decoder_1_out9), .out10(decoder_1_out10), .out11(decoder_1_out11),
    .out12(decoder_1_out12), .out13(decoder_1_out13), .out14(decoder_1_out14),
    .sel({Bit3_Cond, Bit2_Cond, Bit1_Cond, Bit0_Cond}));  // open: out15, en
  Comparator #(.width(1)) comparator_1 (.a(N), .b(V), .eq(comparator_1_eq));  // open: gt, lt
  Comparator #(.width(1)) comparator_2 (.a(N), .b(V), .eq(comparator_2_eq));  // open: gt, lt
  Comparator #(.width(1)) comparator_3 (.a(N), .b(V), .eq(comparator_3_eq));  // open: gt, lt
  Comparator #(.width(1)) comparator_4 (.a(N), .b(V), .eq(comparator_4_eq));  // open: gt, lt
  and and_1 (and_1_out, decoder_1_out0, Z);
  and and_2 (and_2_out, decoder_1_out1, ~Z);  // AND_Gate
  and and_3 (and_3_out, decoder_1_out2, C);
  and and_4 (and_4_out, decoder_1_out3, ~C);  // AND_Gate
  and and_5 (and_5_out, decoder_1_out4, N);
  and and_6 (and_6_out, decoder_1_out5, ~N);  // AND_Gate
  and and_7 (and_7_out, decoder_1_out6, V);
  and and_8 (and_8_out, decoder_1_out7, ~V);  // AND_Gate
  and and_9 (and_9_out, decoder_1_out8, C, ~Z);  // AND_Gate
  and and_10 (and_10_out, decoder_1_out9, ~C, Z);  // AND_Gate
  and and_11 (and_11_out, decoder_1_out10, comparator_1_eq);
  and and_12 (and_12_out, decoder_1_out11, ~comparator_2_eq);  // AND_Gate
  and and_13 (and_13_out, decoder_1_out12, ~Z, comparator_3_eq);  // AND_Gate
  and and_14 (and_14_out, decoder_1_out13, Z, ~comparator_4_eq);  // AND_Gate
  or or_1 (Cond, and_1_out, and_2_out, and_3_out, and_4_out, and_5_out, and_6_out, and_7_out, and_8_out, and_9_out, and_10_out, and_11_out, and_12_out, and_13_out, and_14_out, decoder_1_out14);
endmodule
