// Logisim project Projet_PEP.circ as structural Verilog: 2 circuits, main circuit main
module main (
  input  CarryIn,
  input  in_2
);

  wire clock_1_out, Ld_St, LdS, not_1_out, not_2_out, not_3_out, Reset_out, StS;
  wire [2:0] controller_1_rd, controller_1_rm, controller_1_rn;
  wire [3:0] alu_32_bits_1_p3, controller_1_codeop;
  wire [4:0] controller_1_imm5;
  wire [7:0] controller_1_imm8, controller_1_pc, register_1_q;
  wire [15:0] RandomInstruction, rom_1_data;
  wire [31:0] alu_32_bits_1_p6, banc_registre_1_aout, banc_registre_1_bout, multiplexer_1_out, ram_1_data;

  Controller controller_1 (
    .Load_0_Store_1(Ld_St), .CodeOp(controller_1_codeop), .Rm(controller_1_rm), .Imm5(controller_1_imm5),
    .Rd(controller_1_rd), .Imm8(controller_1_imm8), .Rn(controller_1_rn), .Clk(clock_1_out),
    .Instructions(rom_1_data), .Flags(alu_32_bits_1_p3), .PC(controller_1_pc), .Reset(Reset_out));
  Clock clock_1 (.out(clock_1_out));
  Button Reset (.out(Reset_out));
  Random #(.width(16)) random_1 (.clk(clock_1_out), .out(RandomInstruction));  // open: next, clr
  not not_1 (not_1_out, in_2);
  Register register_1 (.D(controller_1_pc), .en(not_1_out), .Q(register_1_q), .clk(clock_1_out), .clr(Reset_out));
  not not_2 (not_2_out, in_2);
  ROM #(.dataWidth(16)) rom_1 (.addr(register_1_q), .data(rom_1_data), .sel(not_2_out));
  Multiplexer #(.width(32), .enable("false")) multiplexer_1 (
    .in0(alu_32_bits_1_p6), .in1(ram_1_data), .out(multiplexer_1_out), .sel(LdS));
  Banc_Registre banc_registre_1 (
    .DataIn(multiplexer_1_out), .RegtDest(controller_1_rd), .RegA(controller_1_rm), .RegB(controller_1_rn),
    .Clk(clock_1_out), .Reset(Reset_out), .Aout(banc_registre_1_aout), .Bout(banc_registre_1_bout));
  // ALU_32_Bits alu_32_bits_1: pin names not known; wires that end beside it: controller_1_imm5, controller_1_codeop, alu_32_bits_1_p3, banc_registre_1_bout, banc_registre_1_aout, alu_32_bits_1_p6, CarryIn
  Comparator #(.width(1)) comparator_1 (.a(1'b0), .b(Ld_St), .gt(StS), .eq(LdS));  // open: lt
  not not_3 (not_3_out, in_2);
  RAM #(.dataWidth(32), .bus("separate")) ram_1 (
    .addr(controller_1_imm8), .din(banc_registre_1_bout), .data(ram_1_data), .str(StS), .sel(not_3_out),
    .clk(clock_1_out), .ld(LdS), .clr(Reset_out));

  // Other names for the same wires on the sheet: Stop = in_2

  // Notes on the sheet:
  //   contents of rom_1 (hex, n*v repeats v):
  //   284 1a58 2101 4001 4143 6358 68d1 de1a
endmodule

module OldPCManagement (
);

  wire undriven_2, undriven_3, undriven_4;
  wire [7:0] adder_1_out, PC, undriven;

  Adder adder_1 (.a(PC), .b(undriven), .out(adder_1_out));  // open: cin, cout
  Register register_1 (.D(adder_1_out), .en(undriven_2), .Q(PC), .clk(undriven_3), .clr(undriven_4));
endmodule
