// Logisim project RAM.circ as structural Verilog: 1 circuit, main circuit RAM
module RAM (
  input  [7:0] Address,
  input  [31:0] Datain,
  input  sel,
  input  Clk,
  input  Ld,
  input  Clr,
  output [31:0] Dataout
);

  RAM_part #(.dataWidth(32), .bus("separate")) ram_1 (
    .addr(Address), .din(Datain), .data(Dataout), .sel(sel), .clk(Clk), .ld(Ld), .clr(Clr));  // open: str
endmodule
