// Logisim project ROM.circ as structural Verilog: 1 circuit, main circuit ROM
module ROM (
  input  [7:0] Addres,
  input  [15:0] Inst,
  input  sel
);

  ROM_part #(.dataWidth(16)) rom_1 (.addr(Addres), .data(Inst), .sel(sel));
endmodule
